// Digital circuit TEMPT-ALU.dig as structural Verilog
module TEMPT_ALU (
  input  [7:0] A_in,
  input  [7:0] B_in,
  input  [4:0] OpSel,
  input  BusSel,
  output [7:0] A_out,
  output [7:0] B_out,
  output [4:0] flags_out
);

  wire [7:0] add_1_s, multiplexer_1_out, sub_1_s, tmept_ieh_1_dout, tmept_iel_1_dout, tmept_ifb_1_dout,
       tmept_ine_1_dout, tmept_inh_1_dout, tmept_inl_1_dout, tmept_ino_1_dout, tmept_inv_1_dout,
       tmept_iol_1_dout, tmept_rev_1_dout, tmept_rhe_1_dout, tmept_rho_1_dout, tmept_ril_1_dout,
       tmept_rir_1_dout, tmept_rle_1_dout, tmept_rlo_1_dout, tmept_rol_1_dout, tmept_ror_1_dout,
       tmept_rve_1_dout, tmept_rvh_1_dout, tmept_rvo_1_dout, tmept_sol_1_dout, tmept_sor_1_dout,
       tmept_szl_1_dout, tmept_szr_1_dout, tmpet_ilb_1_dout, tmpet_ioh_1_dout, tmpet_rvl_1_dout;

  TMEPT_IEH tmept_ieh_1 (.Din(A_in), .Dout(tmept_ieh_1_dout));
  TMEPT_IEL tmept_iel_1 (.Din(A_in), .Dout(tmept_iel_1_dout));
  TMEPT_IFB tmept_ifb_1 (.Din(A_in), .Dout(tmept_ifb_1_dout));
  TMEPT_INE tmept_ine_1 (.Din(A_in), .Dout(tmept_ine_1_dout));
  TMEPT_INH tmept_inh_1 (.Din(A_in), .Dout(tmept_inh_1_dout));
  TMEPT_INL tmept_inl_1 (.Din(A_in), .Dout(tmept_inl_1_dout));
  TMEPT_INO tmept_ino_1 (.Din(A_in), .Dout(tmept_ino_1_dout));
  TMEPT_INV tmept_inv_1 (.Din(A_in), .Dout(tmept_inv_1_dout));
  TMEPT_IOL tmept_iol_1 (.Din(A_in), .Dout(tmept_iol_1_dout));
  TMEPT_REV tmept_rev_1 (.Din(A_in), .Dout(tmept_rev_1_dout));
  TMEPT_RHE tmept_rhe_1 (.Din(A_in), .Dout(tmept_rhe_1_dout));
  TMEPT_RHO tmept_rho_1 (.Din(A_in), .Dout(tmept_rho_1_dout));
  TMEPT_RIL tmept_ril_1 (.Din(A_in), .Dout(tmept_ril_1_dout));
  TMEPT_RIR tmept_rir_1 (.Din(A_in), .Dout(tmept_rir_1_dout));
  TMEPT_RLE tmept_rle_1 (.Din(A_in), .Dout(tmept_rle_1_dout));
  TMEPT_RLO tmept_rlo_1 (.Din(A_in), .Dout(tmept_rlo_1_dout));
  TMEPT_ROL tmept_rol_1 (.Din(A_in), .Dout(tmept_rol_1_dout));
  TMEPT_ROR tmept_ror_1 (.Din(A_in), .Dout(tmept_ror_1_dout));
  TMEPT_RVE tmept_rve_1 (.Din(A_in), .Dout(tmept_rve_1_dout));
  TMEPT_RVH tmept_rvh_1 (.Din(A_in), .Dout(tmept_rvh_1_dout));
  TMEPT_RVO tmept_rvo_1 (.Din(A_in), .Dout(tmept_rvo_1_dout));
  TMEPT_SOL tmept_sol_1 (.Din(A_in), .Dout(tmept_sol_1_dout));
  TMEPT_SOR tmept_sor_1 (.Din(A_in), .Dout(tmept_sor_1_dout));
  TMEPT_SZL tmept_szl_1 (.Din(A_in), .Dout(tmept_szl_1_dout));
  TMEPT_SZR tmept_szr_1 (.Din(A_in), .Dout(tmept_szr_1_dout));
  TMPET_ILB tmpet_ilb_1 (.Din(A_in), .Dout(tmpet_ilb_1_dout));
  TMPET_IOH tmpet_ioh_1 (.Din(A_in), .Dout(tmpet_ioh_1_dout));
  TMPET_RVL tmpet_rvl_1 (.Din(A_in), .Dout(tmpet_rvl_1_dout));
  Add #(.Bits(8)) add_1 (.a(A_in), .b(B_in), .c_i(1'b0), .s(add_1_s), .c_o(flags_out[0]));
  Sub #(.Bits(8)) sub_1 (.a(A_in), .b(B_in), .c_i(1'b0), .s(sub_1_s), .c_o(flags_out[1]));
  Comparator #(.Bits(8)) comparator_1 (.a(A_in), .b(B_in), .gt(flags_out[2]), .eq(flags_out[3]), .lt(flags_out[4]));
  Multiplexer #(.Bits(8), .Selector_Bits(5)) multiplexer_1 (
    .sel(OpSel), .in_0({8{1'b0}}), .in_1(tmept_ieh_1_dout), .in_2(tmept_iel_1_dout), .in_3(tmept_ifb_1_dout),
    .in_4(tmept_ine_1_dout), .in_5(tmept_inh_1_dout), .in_6(tmept_inl_1_dout), .in_7(tmept_ino_1_dout),
    .in_8(tmept_inv_1_dout), .in_9(tmept_iol_1_dout), .in_10(tmept_rev_1_dout), .in_11(tmept_rhe_1_dout),
    .in_12(tmept_rho_1_dout), .in_13(tmept_ril_1_dout), .in_14(tmept_rir_1_dout), .in_15(tmept_rle_1_dout),
    .in_16(tmept_rlo_1_dout), .in_17(tmept_rol_1_dout), .in_18(tmept_ror_1_dout), .in_19(tmept_rve_1_dout),
    .in_20(tmept_rvh_1_dout), .in_21(tmept_rvo_1_dout), .in_22(tmept_sol_1_dout), .in_23(tmept_sor_1_dout),
    .in_24(tmept_szl_1_dout), .in_25(tmept_szr_1_dout), .in_26(tmpet_ilb_1_dout), .in_27(tmpet_ioh_1_dout),
    .in_28(tmpet_rvl_1_dout), .in_29(add_1_s), .in_30(sub_1_s), .in_31(8'h1), .out(multiplexer_1_out));
  Demultiplexer #(.Bits(8)) demultiplexer_1 (.sel(BusSel), .in(multiplexer_1_out), .out_0(A_out), .out_1(B_out));
endmodule
