// Digital circuit TMEPT-IEH.dig as structural Verilog
module TMEPT_IEH (
  input  [7:0] Din,
  output [7:0] Dout
);

  not not_1 (Dout[7], Din[7]);
  not not_2 (Dout[5], Din[5]);

  assign {Dout[6], Dout[4:0]} = {Din[6], Din[4:0]};
endmodule
