// Digital circuit TMEPT-IEL.dig as structural Verilog
module TMEPT_IEL (
  input  [7:0] Din,
  output [7:0] Dout
);

  not not_1 (Dout[3], Din[3]);
  not not_2 (Dout[1], Din[1]);

  assign {Dout[7:4], Dout[2], Dout[0]} = {Din[7:4], Din[2], Din[0]};
endmodule
