// Digital circuit TMEPT-INE.dig as structural Verilog
module TMEPT_INE (
  input  [7:0] Din,
  output [7:0] Dout
);

  not not_1 (Dout[7], Din[7]);
  not not_2 (Dout[5], Din[5]);
  not not_3 (Dout[3], Din[3]);
  not not_4 (Dout[1], Din[1]);

  assign {Dout[6], Dout[4], Dout[2], Dout[0]} = {Din[6], Din[4], Din[2], Din[0]};
endmodule
