// Digital circuit TMEPT-INH.dig as structural Verilog
module TMEPT_INH (
  input  [7:0] Din,
  output [7:0] Dout
);

  not not_1 (Dout[7], Din[7]);
  not not_2 (Dout[5], Din[5]);
  not not_3 (Dout[6], Din[6]);
  not not_4 (Dout[4], Din[4]);

  assign Dout[3:0] = Din[3:0];
endmodule
