// Digital circuit TMEPT-INL.dig as structural Verilog
module TMEPT_INL (
  input  [7:0] Din,
  output [7:0] Dout
);

  not not_1 (Dout[2], Din[2]);
  not not_2 (Dout[3], Din[3]);
  not not_3 (Dout[0], Din[0]);
  not not_4 (Dout[1], Din[1]);

  assign Dout[7:4] = Din[7:4];
endmodule
