// Digital circuit TMEPT-INO.dig as structural Verilog
module TMEPT_INO (
  input  [7:0] Din,
  output [7:0] Dout
);

  not not_1 (Dout[6], Din[6]);
  not not_2 (Dout[4], Din[4]);
  not not_3 (Dout[2], Din[2]);
  not not_4 (Dout[0], Din[0]);

  assign {Dout[7], Dout[5], Dout[3], Dout[1]} = {Din[7], Din[5], Din[3], Din[1]};
endmodule
