// Digital circuit TMEPT-INV.dig as structural Verilog
module TMEPT_INV (
  input  [7:0] Din,
  output [7:0] Dout
);

  not not_1 (Dout[7], Din[7]);
  not not_2 (Dout[5], Din[5]);
  not not_3 (Dout[6], Din[6]);
  not not_4 (Dout[3], Din[3]);
  not not_5 (Dout[4], Din[4]);
  not not_6 (Dout[1], Din[1]);
  not not_7 (Dout[2], Din[2]);
  not not_8 (Dout[0], Din[0]);
endmodule
