// Digital circuit TMEPT-IOL.dig as structural Verilog
module TMEPT_IOL (
  input  [7:0] Din,
  output [7:0] Dout
);

  not not_1 (Dout[2], Din[2]);
  not not_2 (Dout[0], Din[0]);

  assign {Dout[7:3], Dout[1]} = {Din[7:3], Din[1]};
endmodule
