// Digital circuit TMEPT-REV.dig as structural Verilog
module TMEPT_REV (
  input  [7:0] Din,
  output [7:0] Dout
);


  assign Dout = {Din[0], Din[1], Din[2], Din[3], Din[4], Din[5], Din[6], Din[7]};
endmodule
