// Digital circuit TMEPT-RVE.dig as structural Verilog
module TMEPT_RVE (
  input  [7:0] Din,
  output [7:0] Dout
);


  assign Dout = {Din[1], Din[6], Din[3], Din[4], Din[5], Din[2], Din[7], Din[0]};
endmodule
