// Digital circuit TMEPT-RVO.dig as structural Verilog
module TMEPT_RVO (
  input  [7:0] Din,
  output [7:0] Dout
);


  assign Dout = {Din[7], Din[0], Din[5], Din[2], Din[3], Din[4], Din[1], Din[6]};
endmodule
