// Digital circuit TMPET-IOH.dig as structural Verilog
module TMPET_IOH (
  input  [7:0] Din,
  output [7:0] Dout
);

  not not_1 (Dout[6], Din[6]);
  not not_2 (Dout[4], Din[4]);

  assign {Dout[7], Dout[5], Dout[3:0]} = {Din[7], Din[5], Din[3:0]};
endmodule
